# Fritzing sketch AutoStrap (saved by Fritzing 0.9.3b)
breadboards: 1

parts:
  Driver1 = 28BYJ-48 Driver Module [part_number=ULN2003 package=THT]
  SM1 = 28BYJ-48 Stepper Motor [part_number=28BYJ-48]
  Arduino = Arduino Uno (Rev3)
  VCC1 = Battery block 9V
  C1 = Capacitor Polarized [package=nippon_f80]
  S1 = Pushbutton [package="[THT]"]
  R1 = Resistor [tolerance=±5% resistance=220 package=THT]
  R2 = Resistor [tolerance=±5% resistance=220 package=THT]
  R3 = Resistor [tolerance=±5% resistance=220 package=THT]

nets:
  N1: Driver1.IN1, Arduino.D11_PWM/MOSI
  N2: Driver1.IN2, Arduino.D10_PWM/SS
  N3: Driver1.IN3, Arduino.D9_PWM
  N4: Driver1.IN4, Arduino.D8
  N5: Driver1.blue-pin, SM1.blue-pin
  N6: Driver1.pink-pin, SM1.pink-pin
  N7: Driver1.yellow-pin, SM1.yellow-pin
  N8: Driver1.orange-pin, SM1.orange-pin
  N9: Driver1.red-pin, SM1.red-pin
  N10: Arduino.A0, R2.Pin_0, R3.Pin_0
  N11: Arduino.D2, S1.Pin_1, S1.Pin_2, R1.Pin_0
  N12: Arduino.5V, S1.Pin_3, S1.Pin_4, R2.Pin_1
  N13: Arduino.GND, VCC1.-, C1.-, R1.Pin_1, R3.Pin_1
  N14: Arduino.VIN, VCC1.+, C1.+

notes:
  This resistor with the green wires is the one in the spring! I used a 1k Ohm resistor.

custom parts:
  28BYJ-48 Driver Module: Generic male header
  28BYJ-48 Stepper Motor: Unipolar Stepper Motor 28BYJ-48 Top coil - pink & orange Bottom coil - blue & yellow Common rail - red Connector pins: blue - pink - yellow - orange - red
